// Logisim project ALU.circ as structural Verilog: 3 circuits, main circuit main
module main (
  input  CS2,
  input  CS1,
  input  CS0,
  input  B4,
  input  B3,
  input  B2,
  input  B1,
  input  A4,
  input  A3,
  input  A2,
  input  A1,
  output F1,
  output F2,
  output F3,
  output F4,
  output Cout,
  output z,
  output S,
  output C,
  output V
);

  wire adder_1_cout, adder_2_cout, adder_3_cout, adder_4_cout, and_1_out, and_2_out, and_3_out, and_4_out,
       not_1_out, X1_out, X2_out, X3_out, X4_out, xnor_1_out, xnor_2_out, xnor_3_out, xnor_4_out, Y1_out,
       Y2_out, Y3_out, Y4_out, Z1_out, Z2_out, Z3_out, Z4_out;

  not not_1 (not_1_out, CS1);
  xnor xnor_1 (xnor_1_out, CS2, B1);
  xnor xnor_2 (xnor_2_out, CS2, B2);
  xnor xnor_3 (xnor_3_out, B3, CS2);
  xnor xnor_4 (xnor_4_out, B4, CS2);
  and and_1 (and_1_out, xnor_1_out, CS1);
  and and_2 (and_2_out, xnor_2_out, CS1);
  and and_3 (and_3_out, xnor_3_out, CS1);
  and and_4 (and_4_out, xnor_4_out, CS1);
  or X1 (X1_out, and_1_out, A1);
  nor Y1 (Y1_out, B1, CS2);
  or X2 (X2_out, and_2_out, A2);
  nor Y2 (Y2_out, B2, CS2);
  or X3 (X3_out, and_3_out, A3);
  nor Y3 (Y3_out, B3, CS2);
  or X4 (X4_out, and_4_out, A4);
  nor Y4 (Y4_out, CS2, B4);
  and Z1 (Z1_out, not_1_out, CS0);
  Adder #(.width(1)) adder_1 (.a(X1_out), .b(Y1_out), .out(F1), .cin(Z1_out), .cout(adder_1_cout));
  and Z2 (Z2_out, not_1_out, adder_1_cout);
  Adder #(.width(1)) adder_2 (.a(X2_out), .b(Y2_out), .out(F2), .cin(Z2_out), .cout(adder_2_cout));
  and Z3 (Z3_out, not_1_out, adder_2_cout);
  Adder #(.width(1)) adder_3 (.a(X3_out), .b(Y3_out), .out(F3), .cin(Z3_out), .cout(adder_3_cout));
  and Z4 (Z4_out, not_1_out, adder_3_cout);
  Adder #(.width(1)) adder_4 (.a(X4_out), .b(Y4_out), .out(F4), .cin(Z4_out), .cout(adder_4_cout));
  and and_5 (C, adder_4_cout, not_1_out);
  xor xor_1 (V, Z4_out, C);
  nor nor_1 (z, F1, F2, F3, F4);

  assign Cout = C;
  assign S = F4;
endmodule

module _4_bit_ALU (
  input  CS2,
  input  CS1,
  input  CS0,
  input  B4,
  input  B3,
  input  B2,
  input  B1,
  input  A4,
  input  A3,
  input  A2,
  input  A1,
  output F1,
  output F2,
  output F3,
  output F4,
  output V,
  output Z,
  output S,
  output C
);

  wire adder_1_cout, adder_2_cout, adder_3_cout, and_1_out, and_2_out, and_3_out, and_4_out, not_1_out,
       X1_out, X2_out, X3_out, X4_out, xnor_1_out, xnor_2_out, xnor_3_out, xnor_4_out, Y1_out, Y2_out,
       Y3_out, Y4_out, Z1_out, Z2_out, Z3_out, Z4_out;

  not not_1 (not_1_out, CS1);
  xnor xnor_1 (xnor_1_out, CS2, B1);
  xnor xnor_2 (xnor_2_out, CS2, B2);
  xnor xnor_3 (xnor_3_out, B3, CS2);
  xnor xnor_4 (xnor_4_out, B4, CS2);
  and and_1 (and_1_out, xnor_1_out, CS1);
  and and_2 (and_2_out, xnor_2_out, CS1);
  and and_3 (and_3_out, xnor_3_out, CS1);
  and and_4 (and_4_out, xnor_4_out, CS1);
  or X1 (X1_out, and_1_out, A1);
  nor Y1 (Y1_out, B1, CS2);
  or X2 (X2_out, and_2_out, A2);
  nor Y2 (Y2_out, B2, CS2);
  or X3 (X3_out, and_3_out, A3);
  nor Y3 (Y3_out, B3, CS2);
  or X4 (X4_out, and_4_out, A4);
  nor Y4 (Y4_out, CS2, B4);
  and Z1 (Z1_out, not_1_out, CS0);
  Adder #(.width(1)) adder_1 (.a(X1_out), .b(Y1_out), .out(F1), .cin(Z1_out), .cout(adder_1_cout));
  and Z2 (Z2_out, not_1_out, adder_1_cout);
  Adder #(.width(1)) adder_2 (.a(X2_out), .b(Y2_out), .out(F2), .cin(Z2_out), .cout(adder_2_cout));
  and Z3 (Z3_out, not_1_out, adder_2_cout);
  Adder #(.width(1)) adder_3 (.a(X3_out), .b(Y3_out), .out(F3), .cin(Z3_out), .cout(adder_3_cout));
  and Z4 (Z4_out, not_1_out, adder_3_cout);
  Adder #(.width(1)) adder_4 (.a(X4_out), .b(Y4_out), .out(F4), .cin(Z4_out), .cout(C));
  xor xor_1 (V, Z4_out, C);
  nor nor_1 (Z, F1, F2, F3, F4);

  assign S = F4;
endmodule

module test (
  input  [3:0] B,
  input  [3:0] A,
  input  [2:0] CS,
  output [3:0] F,
  output Cout,
  output [3:0] VZSC
);

  // _4_bit_ALU _4_bit_ALU: pin names not known; wires that end beside it: CS[2], CS[1], CS[0], B[3], VZSC[3], B[2], VZSC[2], B[1], VZSC[1], B[0], VZSC[0], A[3], A[2], A[1], A[0], F[0], F[1], F[2], F[3], Cout
endmodule
