// Logisim project FP_Adder.circ as structural Verilog: 1 circuit, main circuit main
module main (
  input  [15:0] B,
  input  [15:0] A,
  input  [3:0] in_3,
  input  [3:0] in_4,
  input  [3:0] in_5,
  input  [3:0] Increament,
  input  [3:0] in_7,
  input  [3:0] in_8,
  output [3:0] out_9,
  output [1:0] out_10,
  output [12:0] out_11,
  output out_12,
  output [3:0] out_13,
  output [12:0] out_14,
  output [11:0] out_15,
  output [12:0] out_16,
  output [3:0] out_17,
  output [11:0] out_18,
  output [11:0] out_19,
  output [11:0] out_20,
  output [3:0] out_21,
  output [11:0] out_22,
  output [15:0] out_23,
  output Overflow,
  output Underflow
);

  wire adder_4_cout, and_1_out, comparator_1_lt, comparator_2_lt, comparator_4_eq, comparator_4_gt,
       comparator_4_lt, multiplexer_8_out, multiplexer_9_out, not_1_out, or_2_out, xor_9_out;
  wire [3:0] adder_1_out, adder_3_out, bitfinder_1_index, multiplexer_1_out, subtractor_1_out, xor_5_out;
  wire [11:0] bit_extender_1_out, bit_extender_3_out, negator_1_out, shifter_1_out, shifter_2_out, xor_10_out;
  wire [12:0] bit_extender_2_out, bit_extender_4_out, undriven;

  Comparator #(.width(4), .mode("unsigned")) comparator_1 (
    .a(multiplexer_1_out), .b(out_21), .lt(comparator_1_lt));  // open: gt, eq
  or or_1 (Underflow, comparator_1_lt, comparator_2_lt);
  Multiplexer #(.width(4), .enable("false")) multiplexer_1 (
    .in0(B[14:11]), .in1(A[14:11]), .out(multiplexer_1_out), .sel(out_12));
  Subtractor #(.width(4)) subtractor_1 (.a(multiplexer_1_out), .b(out_21), .out(subtractor_1_out));  // open: bin, bout
  Subtractor #(.width(4)) subtractor_2 (.a(in_5), .b(bitfinder_1_index), .out(out_21));  // open: bin, bout
  Adder #(.width(4)) adder_1 (.a(multiplexer_1_out), .b(Increament), .out(adder_1_out));  // open: cin, cout
  Multiplexer #(.width(4), .enable("false")) multiplexer_2 (
    .in0(subtractor_1_out), .in1(adder_1_out), .out(out_23[14:11]), .sel(and_1_out));
  Adder #(.width(4)) adder_2 (.a(A[14:11]), .b(out_9), .out(out_13), .cin(1'b1), .cout(out_12));
  xor xor_1 (out_9[0], 1'b1, B[11]);
  xor xor_2 (out_9[1], 1'b1, B[12]);
  xor xor_3 (out_9[2], 1'b1, B[13]);
  xor xor_4 (out_9[3], 1'b1, B[14]);
  BitFinder #(.width(12), .\type ("high1")) bitfinder_1 (.in(out_18), .index(bitfinder_1_index));  // open: found
  Shifter #(.width(12)) shifter_1 (.in(out_18), .\dist (out_21), .out(shifter_1_out));
  Comparator #(.width(4), .mode("unsigned")) comparator_2 (
    .a(out_23[14:11]), .b(in_8), .lt(comparator_2_lt));  // open: gt, eq
  assign bit_extender_1_out = {{1{1'b1}}, A[10:0]};  // Bit_Extender bit_extender_1
  xor xor_5 (xor_5_out[0], 1'b1, out_13[0]);
  xor xor_6 (xor_5_out[1], 1'b1, out_13[1]);
  xor xor_7 (xor_5_out[2], 1'b1, out_13[2]);
  xor xor_8 (xor_5_out[3], 1'b1, out_13[3]);
  Multiplexer #(.width(12), .enable("false")) multiplexer_3 (
    .in0(shifter_1_out), .in1(shifter_2_out), .out(out_22), .sel(and_1_out));
  assign bit_extender_2_out = {{1{1'b0}}, bit_extender_1_out};  // Bit_Extender bit_extender_2
  Comparator #(.width(4), .mode("unsigned")) comparator_3 (.a(in_7), .b(out_23[14:11]), .lt(Overflow));  // open: gt, eq
  Multiplexer #(.width(13), .enable("false")) multiplexer_4 (
    .in0(bit_extender_4_out), .in1(bit_extender_2_out), .out(out_11), .sel(out_12));
  Adder #(.width(4)) adder_3 (.a(xor_5_out), .b(in_3), .out(adder_3_out), .cin(1'b1));  // open: cout
  Shifter #(.width(12), .shift("lr")) shifter_2 (.in(out_18), .\dist (in_4), .out(shifter_2_out));
  Multiplexer #(.width(13), .enable("false")) multiplexer_5 (
    .in0(bit_extender_2_out), .in1(bit_extender_4_out), .out(out_14), .sel(out_12));
  Multiplexer #(.width(4), .enable("false")) multiplexer_6 (
    .in0(adder_3_out), .in1(out_13), .out(out_17), .sel(out_12));
  and and_1 (and_1_out, adder_4_cout, out_18[11]);
  Shifter #(.width(13), .shift("lr")) shifter_3 (.in(out_14), .\dist (out_17), .out(out_16));
  assign bit_extender_3_out = {{1{1'b1}}, B[10:0]};  // Bit_Extender bit_extender_3
  Adder #(.width(12)) adder_4 (.a(out_19), .b(out_20), .out(out_18), .cout(adder_4_cout));  // open: cin
  assign bit_extender_4_out = {{1{1'b0}}, bit_extender_3_out};  // Bit_Extender bit_extender_4
  Multiplexer #(.width(12), .enable("false")) multiplexer_7 (
    .in0(out_11[11:0]), .in1(negator_1_out), .out(out_19), .sel(multiplexer_8_out));
  Negator #(.width(12)) negator_1 (.in(out_11[11:0]), .out(negator_1_out));
  xor xor_9 (xor_9_out, A[15], B[15]);
  Multiplexer #(.enable("false")) multiplexer_8 (.in0(1'b0), .in1(A[15]), .out(multiplexer_8_out), .sel(xor_9_out));
  Multiplexer #(.enable("false")) multiplexer_9 (.in0(1'b0), .in1(B[15]), .out(multiplexer_9_out), .sel(xor_9_out));
  Negator #(.width(12)) negator_2 (.in(out_16[11:0]), .out(out_15));
  Multiplexer #(.width(12), .enable("false")) multiplexer_10 (
    .in0(out_16[11:0]), .in1(out_15), .out(out_20), .sel(multiplexer_9_out));
  Multiplexer #(.select(2), .enable("false")) multiplexer_11 (
    .in0(1'b0), .in1(not_1_out), .in2(comparator_4_lt), .in3(1'b1), .out(out_23[15]), .sel({A[15], B[15]}));
  Comparator #(.width(12), .mode("unsigned")) comparator_4 (
    .a(out_11[11:0]), .b(out_16[11:0]), .gt(comparator_4_gt), .eq(comparator_4_eq), .lt(comparator_4_lt));
  not not_1 (not_1_out, or_2_out);
  or or_2 (or_2_out, comparator_4_gt, comparator_4_eq);
  xor xor_10 (xor_10_out[0], undriven[0], 1'b1);
  xor xor_11 (xor_10_out[1], undriven[1], 1'b1);
  xor xor_12 (xor_10_out[2], undriven[2], 1'b1);
  xor xor_13 (xor_10_out[3], undriven[3], 1'b1);
  xor xor_14 (xor_10_out[4], undriven[4], 1'b1);
  xor xor_15 (xor_10_out[5], undriven[5], 1'b1);
  xor xor_16 (xor_10_out[6], undriven[6], 1'b1);
  xor xor_17 (xor_10_out[7], undriven[7], 1'b1);
  xor xor_18 (xor_10_out[8], undriven[8], 1'b1);
  xor xor_19 (xor_10_out[9], undriven[9], 1'b1);
  xor xor_20 (xor_10_out[10], undriven[10], 1'b1);
  xor xor_21 (xor_10_out[11], undriven[12], 1'b1);

  assign out_10 = {A[15], B[15]};
  assign out_23[10:0] = out_22[10:0];

  // Notes on the sheet:
  //   Sign(A)
  //   Decreament
  //   Exponent(A)
  //   Left Shift
  //   Fraction(A)
  //   Right Shift
  //   Sign(B)
  //   Larger
  //   Exponent(B)
  //   Smaller
  //   Fraction(B)
  //   Addition Result
  //   If both signs are same, then pass it directly otherwise to negator
endmodule
