// Logisim project MIPS.circ as structural Verilog: 1 circuit, main circuit main
module main (
  output [11:0] out_1,
  output [19:0] out_2,
  output [7:0] out_3,
  output [7:0] out_4,
  output [7:0] out_5
);

  wire alu_1_p4, and_1_out, and_2_out, clock_1_out, multiplexer_5_out, not_1_out;
  wire [3:0] multiplexer_1_out, multiplexer_2_out;
  wire [7:0] adder_1_out, adder_2_out, alu_1_p5, bit_extender_1_out, multiplexer_4_out, multiplexer_6_out,
       multiplexer_8_out, ram_1_data, register_1_q, register_file_1_p1;

  Clock clock_1 (.out(clock_1_out));
  Register register_1 (.D(multiplexer_8_out), .Q(register_1_q), .clk(clock_1_out));  // open: en, clr
  Adder adder_1 (.a(8'h1), .b(register_1_q), .out(adder_1_out));  // open: cin, cout
  ROM #(.dataWidth(20)) rom_1 (.addr(register_1_q), .data(out_2));  // open: sel
  assign bit_extender_1_out = {{4{1'b0}}, out_2[3:0]};  // Bit_Extender bit_extender_1
  Multiplexer #(.width(4), .enable("false")) multiplexer_1 (
    .in0(out_2[15:12]), .in1(out_2[11:8]), .out(multiplexer_1_out), .sel(out_1[11]));
  Multiplexer #(.width(4), .enable("false")) multiplexer_2 (
    .in0(out_2[11:8]), .in1(out_2[7:4]), .out(multiplexer_2_out), .sel(out_1[10]));
  Multiplexer #(.width(8), .enable("false")) multiplexer_3 (
    .in0(out_2[7:0]), .in1(bit_extender_1_out), .out(out_5), .sel(out_1[11]));
  ROM #(.addrWidth(4), .dataWidth(12)) rom_2 (.addr(out_2[19:16]), .data(out_1));  // open: sel
  // Register_File register_file_1: pin names not known; wires that end beside it: register_file_1_p1, multiplexer_1_out, out_2[11:8], multiplexer_2_out, clock_1_out, out_1[8], out_3, out_4
  Multiplexer #(.width(8), .enable("false")) multiplexer_4 (
    .in0(out_4), .in1(out_5), .out(multiplexer_4_out), .sel(out_1[9]));
  // ALU alu_1: pin names not known; wires that end beside it: out_3, multiplexer_4_out, out_1[2:0], alu_1_p4, alu_1_p5
  Adder adder_2 (.a(adder_1_out), .b(out_5), .out(adder_2_out));  // open: cin, cout
  Multiplexer #(.enable("false")) multiplexer_5 (
    .in0(and_1_out), .in1(and_2_out), .out(multiplexer_5_out), .sel(out_1[4]));
  and and_1 (and_1_out, out_1[5], alu_1_p4);
  RAM #(.bus("separate")) ram_1 (
    .addr(alu_1_p5), .din(out_4), .data(ram_1_data), .str(out_1[6]), .clk(clock_1_out), .ld(out_1[7]));  // open: sel, clr
  Multiplexer #(.width(8), .enable("false")) multiplexer_6 (
    .in0(adder_1_out), .in1(adder_2_out), .out(multiplexer_6_out), .sel(multiplexer_5_out));
  and and_2 (and_2_out, out_1[5], not_1_out);
  not not_1 (not_1_out, alu_1_p4);
  Multiplexer #(.width(8), .enable("false")) multiplexer_7 (
    .in0(alu_1_p5), .in1(ram_1_data), .out(register_file_1_p1), .sel(out_1[7]));
  Multiplexer #(.width(8), .enable("false")) multiplexer_8 (
    .in0(multiplexer_6_out), .in1(out_2[15:8]), .out(multiplexer_8_out), .sel(out_1[3]));

  // Notes on the sheet:
  //   contents of rom_1 (hex, n*v repeats v):
  //   71110 71100 72201 72200 41230 73300 83304 73300 84409 74400 d3450 75500 b11bb 71100 61230 73300
  //   34467 74400 f4510 71100 52220 72200 113 71100 e0222 72200 92400 a2300 73300 21204 21303 11103 12204
  //   c0c00
  //   RegWrite
  //   Shift
  //   contents of rom_2 (hex, n*v repeats v):
  //   f05 31 21 302 500 504 503 300 301 240 380 303 f 501 f06 502
  //   RegDst
  //   ALUOp
  //   ALUSrc
  //   Jump
  //   Beqone
  //   Branch
  //   MemToReg
  //   MemWrite
  //   MemRead
endmodule
