// Logisim project Pipelining.circ as structural Verilog: 2 circuits, main circuit main
module main (
  input  Reg_INIT,
  input  Reg_INIT_clock,
  input  [3:0] Reg_INIT_num,
  input  [7:0] Reg_INIT_data
);

  wire clock_1_out;
  wire [1:0] forwarding_unit_1_forwarda, forwarding_unit_1_forwardb, register_4_q, register_10_q;
  wire [2:0] register_3_q;
  wire [3:0] register_7_q, register_8_q, register_9_q, register_13_q, register_15_q;
  wire [7:0] adder_1_out, alu_1_f, multiplexer_1_out, multiplexer_2_out, register_1_q, register_5_q,
       register_6_q, register_11_q, register_12_q, register_14_q, register_file_1_read_data_1,
       register_file_1_read_data_2;
  wire [11:0] rom_2_data;
  wire [19:0] register_2_q, rom_1_data;

  Clock clock_1 (.out(clock_1_out));
  Register register_1 (.D(adder_1_out), .Q(register_1_q), .clk(clock_1_out));  // open: en, clr
  Adder adder_1 (.a(8'h1), .b(register_1_q), .out(adder_1_out));  // open: cin, cout
  ROM #(.dataWidth(20)) rom_1 (.addr(register_1_q), .data(rom_1_data));  // open: sel
  Register #(.width(20)) register_2 (.D(rom_1_data), .Q(register_2_q), .clk(clock_1_out));  // open: en, clr
  ROM #(.addrWidth(4), .dataWidth(12)) rom_2 (.addr(register_2_q[19:16]), .data(rom_2_data));  // open: sel
  Register_File register_file_1 (
    .Write_Data(register_14_q), .Init_tWrite_Data(Reg_INIT_data), .Read_Reg1(register_2_q[15:12]),
    .Read_Reg2(register_2_q[11:8]), .Write_Reg(register_15_q), .init_Write_Reg(Reg_INIT_num),
    .Reg_clock(clock_1_out), .Init_Reg_clock(Reg_INIT_clock), .reg_init(Reg_INIT), .RegWrite(rom_2_data[8]),
    .Read_Data_1(register_file_1_read_data_1), .Read_Data_2(register_file_1_read_data_2));  // open: Error_Write_to_0
  Register #(.width(3)) register_3 (.D(rom_2_data[2:0]), .Q(register_3_q), .clk(clock_1_out));  // open: en, clr
  Register #(.width(2)) register_4 (.D(rom_2_data[7:6]), .Q(register_4_q), .clk(clock_1_out));  // open: en, clr
  Register register_5 (.D(register_file_1_read_data_1), .Q(register_5_q), .clk(clock_1_out));  // open: en, clr
  Register register_6 (.D(register_file_1_read_data_2), .Q(register_6_q), .clk(clock_1_out));  // open: en, clr
  Register #(.width(4)) register_7 (.D(register_2_q[7:4]), .Q(register_7_q), .clk(clock_1_out));  // open: en, clr
  Register #(.width(4)) register_8 (.D(register_2_q[15:12]), .Q(register_8_q));  // open: en, clk, clr
  Register #(.width(4)) register_9 (.D(register_2_q[11:8]), .Q(register_9_q));  // open: en, clk, clr
  Multiplexer #(.select(2), .width(8), .enable("false")) multiplexer_1 (
    .in0(register_5_q), .in1(register_14_q), .in2(register_11_q), .out(multiplexer_1_out),
    .sel(forwarding_unit_1_forwarda));  // open: in3
  Multiplexer #(.select(2), .width(8), .enable("false")) multiplexer_2 (
    .in0(register_6_q), .in1(register_14_q), .in2(register_11_q), .out(multiplexer_2_out),
    .sel(forwarding_unit_1_forwardb));  // open: in3
  Forwarding_Unit forwarding_unit_1 (
    .ID_EX_RS(register_8_q), .ID_EX_RT(register_9_q), .EX_MEM_RegWrite(1'b1), .EX_MEM_RegRd(register_13_q),
    .MEM_WB_RegWrite(1'b1), .MEM_WB_RegRd(register_15_q), .ForwardA(forwarding_unit_1_forwarda),
    .ForwardB(forwarding_unit_1_forwardb));
  ALU alu_1 (
    .A(multiplexer_1_out), .B(multiplexer_2_out), .ALUop(register_3_q), .F(alu_1_f));  // open: overflow, negative, ZF
  Register #(.width(2)) register_10 (.D(register_4_q), .Q(register_10_q), .clk(clock_1_out));  // open: en, clr
  Register register_11 (.D(alu_1_f), .Q(register_11_q), .clk(clock_1_out));  // open: en, clr
  Register register_12 (.D(register_6_q), .Q(register_12_q), .clk(clock_1_out));  // open: en, clr
  Register #(.width(4)) register_13 (.D(register_7_q), .Q(register_13_q), .clk(clock_1_out));  // open: en, clr
  RAM #(.bus("separate")) ram_1 (
    .addr(register_11_q), .din(register_12_q), .str(register_10_q[0]), .clk(clock_1_out),
    .ld(register_10_q[1]));  // open: data, sel, clr
  Register register_14 (.D(register_11_q), .Q(register_14_q), .clk(clock_1_out));  // open: en, clr
  Register #(.width(4)) register_15 (.D(register_13_q), .Q(register_15_q), .clk(clock_1_out));  // open: en, clr

  // Notes on the sheet:
  //   contents of rom_1 (hex, n*v repeats v):
  //   777ff 43420 d3510 62150 f3420 54420 32a e0542 832fc 732f6 b32f6 332f6 932fc a530a 97200 87701 76203
  //   97600 87701 a7300 77701 23200 114f0 c0000 c0700 c1600
  //   IF/ID
  //   contents of rom_2 (hex, n*v repeats v):
  //   f05 31 21 302 500 504 503 300 301 240 380 303 f 501 f06 502
  //   RegWrite
  //   ID/EX
  //   ALUOp
  //   EX/MEM
  //   MemWrite
  //   MemRead
  //   MEM/WB
endmodule

module Forwarding_Unit (
  input  [3:0] ID_EX_RS,
  input  [3:0] ID_EX_RT,
  input  EX_MEM_RegWrite,
  input  [3:0] EX_MEM_RegRd,
  input  MEM_WB_RegWrite,
  input  [3:0] MEM_WB_RegRd,
  output [1:0] ForwardA,
  output [1:0] ForwardB
);

  wire comparator_1_eq, comparator_2_eq, comparator_3_eq, comparator_4_eq, comparator_5_eq, comparator_6_eq,
       comparator_7_eq, comparator_8_eq, not_1_out, not_2_out, not_3_out, not_4_out, not_5_out, not_6_out;

  Comparator #(.width(4)) comparator_1 (.a(EX_MEM_RegRd), .b(4'b0000), .eq(comparator_1_eq));  // open: gt, lt
  Comparator #(.width(4)) comparator_2 (.a(EX_MEM_RegRd), .b(ID_EX_RS), .eq(comparator_2_eq));  // open: gt, lt
  Comparator #(.width(4)) comparator_3 (.a(ID_EX_RS), .b(MEM_WB_RegRd), .eq(comparator_3_eq));  // open: gt, lt
  Comparator #(.width(4)) comparator_4 (.a(MEM_WB_RegRd), .b(4'b0000), .eq(comparator_4_eq));  // open: gt, lt
  Comparator #(.width(4)) comparator_5 (.a(EX_MEM_RegRd), .b(ID_EX_RT), .eq(comparator_5_eq));  // open: gt, lt
  Comparator #(.width(4)) comparator_6 (.a(EX_MEM_RegRd), .b(4'b0000), .eq(comparator_6_eq));  // open: gt, lt
  Comparator #(.width(4)) comparator_7 (.a(MEM_WB_RegRd), .b(ID_EX_RT), .eq(comparator_7_eq));  // open: gt, lt
  Comparator #(.width(4)) comparator_8 (.a(MEM_WB_RegRd), .b(4'b0000), .eq(comparator_8_eq));  // open: gt, lt
  not not_1 (not_1_out, comparator_1_eq);
  not not_2 (not_2_out, comparator_4_eq);
  not not_3 (not_3_out, comparator_6_eq);
  not not_4 (not_4_out, ForwardB[1]);
  not not_5 (not_5_out, comparator_8_eq);
  and and_1 (ForwardA[1], EX_MEM_RegWrite, not_1_out, comparator_2_eq);
  not not_6 (not_6_out, ForwardA[1]);
  and and_2 (ForwardA[0], not_6_out, MEM_WB_RegWrite, comparator_3_eq, not_2_out);
  and and_3 (ForwardB[1], EX_MEM_RegWrite, comparator_5_eq, not_3_out);
  and and_4 (ForwardB[0], not_4_out, comparator_7_eq, not_5_out, MEM_WB_RegWrite);
endmodule
